# Fritzing sketch Fritzing Sketch (saved by Fritzing 0.9.3b)
breadboards: 1

parts:
  Part1 = Arduino Uno (Rev3)
  R1 = Resistor [tolerance=±5% resistance=10k package="1206 [SMD]"]
  R2 = Resistor [tolerance=±5% resistance=1k package="1206 [SMD]"]
  R3 = Resistor [tolerance=±5% resistance=1k package="1206 [SMD]"]
  R4 = Resistor [tolerance=±5% resistance=1k package="1206 [SMD]"]
  R5 = Resistor [tolerance=±5% resistance=1k package="1206 [SMD]"]
  R6 = Resistor [tolerance=±5% resistance=330 package="1206 [SMD]"]
  R7 = Resistor [tolerance=±5% resistance=330 package="1206 [SMD]"]
  R8 = Resistor [tolerance=±5% resistance=330 package="1206 [SMD]"]
  hc-sr1 = hc-sr04
  J1 = Piezo Speaker

nets:
  N1: Part1.A0, R5.Pin_0
  N2: Part1.D9_PWM, hc-sr1.Trig
  N3: Part1.D10_PWM/SS, hc-sr1.Echo
  N4: Part1.D11_PWM/MOSI, J1.pin2
  5V: Part1.5V, R1.Pin_0, hc-sr1.VCC
  GND: Part1.GND, R8.Pin_1, hc-sr1.GND, J1.pin1
  N5: R1.Pin_1, R2.Pin_0, R5.Pin_1
  N6: R2.Pin_1, R3.Pin_0
  N7: R3.Pin_1, R4.Pin_0
  N8: R6.Pin_1, R7.Pin_0
  N9: R7.Pin_1, R8.Pin_0

notes:
  D # 0 *
  C 9 8 7
  B 6 5 4
  A 3 2 1
  (Dibalik)
